# Fritzing sketch IDA3document#1 (saved by Fritzing 0.7.10b)
breadboards: 3

parts:
  Part1 = Thumb Joystick
  LED1 = LED - 5mm [color="Green (565nm)" package="5 mm [THT]"]
  LED2 = LED - 5mm [color="Red (633nm)" package="5 mm [THT]"]
  LED3 = LED - 5mm [color="Yellow (585nm)" package="5 mm [THT]"]
  R2 = Resistor [tolerance=±5% resistance=220 package=THT]
  LED4 = LED - 5mm [color="Green (565nm)" package="5 mm [THT]"]
  LED5 = LED - 5mm [color="Green (565nm)" package="5 mm [THT]"]
  LED6 = LED - 5mm [color="Yellow (585nm)" package="5 mm [THT]"]
  LED7 = LED - 5mm [color="Yellow (585nm)" package="5 mm [THT]"]
  LED8 = LED - 5mm [color="Red (633nm)" package="5 mm [THT]"]
  Arduino1 = Arduino
  R1 = Resistor [tolerance=±5% resistance=220 package=THT]

nets:
  GND: Part1.GND, LED1.cathode, LED4.cathode, LED5.cathode, Arduino1.GND, Arduino1.D9, Arduino1.D8
  N1: Part1.SEL, Arduino1.D2
  N2: Part1.HORZ, Arduino1.A1
  N3: Part1.VERT, Arduino1.A0
  VCC: Part1.VCC, Arduino1.+5V
  N4: LED1.anode, LED2.anode, R2.Pin_0, LED4.anode, LED5.anode, LED7.anode, LED8.anode, Arduino1.D11, Arduino1.3V3, R1.Pin_0
  N5: LED2.cathode, Arduino1.D5
  N6: LED3.cathode, Arduino1.D7
  N7: LED3.anode, R1.Pin_1
  N8: R2.Pin_1, LED6.anode
  N9: LED6.cathode, Arduino1.D10
  N10: LED7.cathode, Arduino1.D12
  N11: LED8.cathode, Arduino1.D6
